// Logisim project ULA 32bits.circ as structural Verilog: 8 circuits, main circuit Célula
module \Célula  (
  input  ESQUERDA,
  input  DIREITA,
  input  A,
  input  B,
  input  [4:0] in_5,
  input  VEM_1,
  output S,
  output VAI_1
);

  wire adder_1_cout, adder_1_out, and_1_out, and_2_out, nand_1_out, or_1_out, subtractor_1_bout,
       subtractor_1_out, xor_1_out;

  and and_1 (and_1_out, A, B);
  or or_1 (or_1_out, A, B);
  nand nand_1 (nand_1_out, A, B);
  xor xor_1 (xor_1_out, A, B);
  Adder #(.width(1)) adder_1 (.a(A), .b(B), .out(adder_1_out), .cin(VEM_1), .cout(adder_1_cout));
  Subtractor #(.width(1)) subtractor_1 (.a(A), .b(B), .out(subtractor_1_out), .bin(VEM_1), .bout(subtractor_1_bout));
  and and_2 (and_2_out, ~in_5[4], ~in_5[3], in_5[2], in_5[1], ~in_5[0]);  // AND_Gate
  Multiplexer multiplexer_1 (.in0(adder_1_cout), .in1(subtractor_1_bout), .out(VAI_1), .sel(and_2_out));  // open: en
  Multiplexer #(.select(5), .enable("false")) multiplexer_2 (
    .in0(and_1_out), .in1(or_1_out), .in2(nand_1_out), .in3(xor_1_out), .in4(adder_1_out), .in5(adder_1_out),
    .in6(subtractor_1_out), .in7(DIREITA), .in8(DIREITA), .in9(ESQUERDA), .out(S), .sel(in_5));  // open: in10, in11, in12, in13, in14, in15, in16, in17, in18, in19, in20, in21, in22, in23, in24, in25, in26, in27, in28, in29, in30, in31
endmodule

module ULA (
  input  [31:0] A,
  input  [4:0] SELETOR,
  input  [31:0] B,
  input  in_4,
  output OVERFLOW,
  output [31:0] S
);

  wire and_1_out, and_2_out, \célula_1_vai_1 , \célula_2_vai_1 , \célula_3_vai_1 , \célula_4_vai_1 ,
       \célula_5_vai_1 , \célula_6_vai_1 , \célula_7_vai_1 , \célula_8_vai_1 , \célula_9_vai_1 ,
       \célula_10_vai_1 , \célula_11_vai_1 , \célula_12_vai_1 , \célula_13_vai_1 , \célula_14_vai_1 ,
       \célula_15_vai_1 , \célula_16_vai_1 , \célula_17_vai_1 , \célula_18_vai_1 , \célula_19_vai_1 ,
       \célula_20_vai_1 , \célula_21_vai_1 , \célula_22_vai_1 , \célula_23_vai_1 , \célula_24_vai_1 ,
       \célula_25_vai_1 , \célula_26_vai_1 , \célula_27_vai_1 , \célula_28_vai_1 , \célula_29_vai_1 ,
       \célula_30_vai_1 , \célula_31_vai_1 , \célula_mais_significativa_1_vai_1 , multiplexer_1_out,
       overflow_fora_1_out_4;

  \Célula_mais_significativa  \célula_mais_significativa_1  (
    .ESQUERDA(A[30]), .A(A[31]), .B(B[31]), .VEM_1(\célula_1_vai_1 ), .in_5(SELETOR),
    .\DIREITA_ARITMÉTICA (A[31]), .DIREITA(1'b0), .S(S[31]), .VAI_1(\célula_mais_significativa_1_vai_1 ));
  Multiplexer #(.enable("false")) multiplexer_1 (
    .in0(overflow_fora_1_out_4), .in1(\célula_mais_significativa_1_vai_1 ), .out(multiplexer_1_out),
    .sel(and_1_out));
  and and_1 (and_1_out, ~SELETOR[0], ~SELETOR[1], SELETOR[2], ~SELETOR[3], ~SELETOR[4]);  // AND_Gate
  Overflow_fora overflow_fora_1 (.A(A[31]), .B(B[31]), .S(S[31]), .out_4(overflow_fora_1_out_4));
  \Célula  \célula_1  (
    .ESQUERDA(A[29]), .A(A[30]), .B(B[30]), .VEM_1(\célula_2_vai_1 ), .in_5(SELETOR), .DIREITA(A[31]),
    .S(S[30]), .VAI_1(\célula_1_vai_1 ));
  \Célula  \célula_2  (
    .ESQUERDA(A[28]), .A(A[29]), .B(B[29]), .VEM_1(\célula_3_vai_1 ), .in_5(SELETOR), .DIREITA(A[30]),
    .S(S[29]), .VAI_1(\célula_2_vai_1 ));
  \Célula  \célula_3  (
    .ESQUERDA(A[27]), .A(A[28]), .B(B[28]), .VEM_1(\célula_4_vai_1 ), .in_5(SELETOR), .DIREITA(A[29]),
    .S(S[28]), .VAI_1(\célula_3_vai_1 ));
  \Célula  \célula_4  (
    .ESQUERDA(A[26]), .A(A[27]), .B(B[27]), .VEM_1(\célula_5_vai_1 ), .in_5(SELETOR), .DIREITA(A[28]),
    .S(S[27]), .VAI_1(\célula_4_vai_1 ));
  \Célula  \célula_5  (
    .ESQUERDA(A[25]), .A(A[26]), .B(B[26]), .VEM_1(\célula_6_vai_1 ), .in_5(SELETOR), .DIREITA(A[27]),
    .S(S[26]), .VAI_1(\célula_5_vai_1 ));
  \Célula  \célula_6  (
    .ESQUERDA(A[24]), .A(A[25]), .B(B[25]), .VEM_1(\célula_7_vai_1 ), .in_5(SELETOR), .DIREITA(A[26]),
    .S(S[25]), .VAI_1(\célula_6_vai_1 ));
  \Célula  \célula_7  (
    .ESQUERDA(A[23]), .A(A[24]), .B(B[24]), .VEM_1(\célula_8_vai_1 ), .in_5(SELETOR), .DIREITA(A[25]),
    .S(S[24]), .VAI_1(\célula_7_vai_1 ));
  \Célula  \célula_8  (
    .ESQUERDA(A[22]), .A(A[23]), .B(B[23]), .VEM_1(\célula_9_vai_1 ), .in_5(SELETOR), .DIREITA(A[24]),
    .S(S[23]), .VAI_1(\célula_8_vai_1 ));
  \Célula  \célula_9  (
    .ESQUERDA(A[21]), .A(A[22]), .B(B[22]), .VEM_1(\célula_10_vai_1 ), .in_5(SELETOR), .DIREITA(A[23]),
    .S(S[22]), .VAI_1(\célula_9_vai_1 ));
  \Célula  \célula_10  (
    .ESQUERDA(A[20]), .A(A[21]), .B(B[21]), .VEM_1(\célula_11_vai_1 ), .in_5(SELETOR), .DIREITA(A[22]),
    .S(S[21]), .VAI_1(\célula_10_vai_1 ));
  \Célula  \célula_11  (
    .ESQUERDA(A[19]), .A(A[20]), .B(B[20]), .VEM_1(\célula_12_vai_1 ), .in_5(SELETOR), .DIREITA(A[21]),
    .S(S[20]), .VAI_1(\célula_11_vai_1 ));
  \Célula  \célula_12  (
    .ESQUERDA(A[18]), .A(A[19]), .B(B[19]), .VEM_1(\célula_13_vai_1 ), .in_5(SELETOR), .DIREITA(A[20]),
    .S(S[19]), .VAI_1(\célula_12_vai_1 ));
  \Célula  \célula_13  (
    .ESQUERDA(A[17]), .A(A[18]), .B(B[18]), .VEM_1(\célula_14_vai_1 ), .in_5(SELETOR), .DIREITA(A[19]),
    .S(S[18]), .VAI_1(\célula_13_vai_1 ));
  \Célula  \célula_14  (
    .ESQUERDA(A[16]), .A(A[17]), .B(B[17]), .VEM_1(\célula_15_vai_1 ), .in_5(SELETOR), .DIREITA(A[18]),
    .S(S[17]), .VAI_1(\célula_14_vai_1 ));
  \Célula  \célula_15  (
    .ESQUERDA(A[15]), .A(A[16]), .B(B[16]), .VEM_1(\célula_16_vai_1 ), .in_5(SELETOR), .DIREITA(A[17]),
    .S(S[16]), .VAI_1(\célula_15_vai_1 ));
  \Célula  \célula_16  (
    .ESQUERDA(A[14]), .A(A[15]), .B(B[15]), .VEM_1(\célula_17_vai_1 ), .in_5(SELETOR), .DIREITA(A[16]),
    .S(S[15]), .VAI_1(\célula_16_vai_1 ));
  \Célula  \célula_17  (
    .ESQUERDA(A[13]), .A(A[14]), .B(B[14]), .VEM_1(\célula_18_vai_1 ), .in_5(SELETOR), .DIREITA(A[15]),
    .S(S[14]), .VAI_1(\célula_17_vai_1 ));
  \Célula  \célula_18  (
    .ESQUERDA(A[12]), .A(A[13]), .B(B[13]), .VEM_1(\célula_19_vai_1 ), .in_5(SELETOR), .DIREITA(A[14]),
    .S(S[13]), .VAI_1(\célula_18_vai_1 ));
  \Célula  \célula_19  (
    .ESQUERDA(A[11]), .A(A[12]), .B(B[12]), .VEM_1(\célula_20_vai_1 ), .in_5(SELETOR), .DIREITA(A[13]),
    .S(S[12]), .VAI_1(\célula_19_vai_1 ));
  \Célula  \célula_20  (
    .ESQUERDA(A[10]), .A(A[11]), .B(B[11]), .VEM_1(\célula_21_vai_1 ), .in_5(SELETOR), .DIREITA(A[12]),
    .S(S[11]), .VAI_1(\célula_20_vai_1 ));
  \Célula  \célula_21  (
    .ESQUERDA(A[9]), .A(A[10]), .B(B[10]), .VEM_1(\célula_22_vai_1 ), .in_5(SELETOR), .DIREITA(A[11]),
    .S(S[10]), .VAI_1(\célula_21_vai_1 ));
  \Célula  \célula_22  (
    .ESQUERDA(A[8]), .A(A[9]), .B(B[9]), .VEM_1(\célula_23_vai_1 ), .in_5(SELETOR), .DIREITA(A[10]),
    .S(S[9]), .VAI_1(\célula_22_vai_1 ));
  \Célula  \célula_23  (
    .ESQUERDA(A[7]), .A(A[8]), .B(B[8]), .VEM_1(\célula_24_vai_1 ), .in_5(SELETOR), .DIREITA(A[9]), .S(S[8]),
    .VAI_1(\célula_23_vai_1 ));
  \Célula  \célula_24  (
    .ESQUERDA(A[6]), .A(A[7]), .B(B[7]), .VEM_1(\célula_25_vai_1 ), .in_5(SELETOR), .DIREITA(A[8]), .S(S[7]),
    .VAI_1(\célula_24_vai_1 ));
  \Célula  \célula_25  (
    .ESQUERDA(A[5]), .A(A[6]), .B(B[6]), .VEM_1(\célula_26_vai_1 ), .in_5(SELETOR), .DIREITA(A[7]), .S(S[6]),
    .VAI_1(\célula_25_vai_1 ));
  \Célula  \célula_26  (
    .ESQUERDA(A[4]), .A(A[5]), .B(B[5]), .VEM_1(\célula_27_vai_1 ), .in_5(SELETOR), .DIREITA(A[6]), .S(S[5]),
    .VAI_1(\célula_26_vai_1 ));
  and and_2 (and_2_out, ~S[31], ~S[30], ~S[29], ~S[28], ~S[27], ~S[26], ~S[25], ~S[24], ~S[23], ~S[22], ~S[21], ~S[20], ~S[19], ~S[18], ~S[17], ~S[16], ~S[15], ~S[14], ~S[13], ~S[12], ~S[11], ~S[10], ~S[9], ~S[8], ~S[7], ~S[6], ~S[5], ~S[4], ~S[3], ~S[2], ~S[1], ~S[0]);  // AND_Gate
  \Célula  \célula_27  (
    .ESQUERDA(A[3]), .A(A[4]), .B(B[4]), .VEM_1(\célula_28_vai_1 ), .in_5(SELETOR), .DIREITA(A[5]), .S(S[4]),
    .VAI_1(\célula_27_vai_1 ));
  \Célula  \célula_28  (
    .ESQUERDA(A[2]), .A(A[3]), .B(B[3]), .VEM_1(\célula_29_vai_1 ), .in_5(SELETOR), .DIREITA(A[4]), .S(S[3]),
    .VAI_1(\célula_28_vai_1 ));
  \Célula  \célula_29  (
    .ESQUERDA(A[1]), .A(A[2]), .B(B[2]), .VEM_1(\célula_30_vai_1 ), .in_5(SELETOR), .DIREITA(A[3]), .S(S[2]),
    .VAI_1(\célula_29_vai_1 ));
  \Célula  \célula_30  (
    .ESQUERDA(A[0]), .A(A[1]), .B(B[1]), .VEM_1(\célula_31_vai_1 ), .in_5(SELETOR), .DIREITA(A[2]), .S(S[1]),
    .VAI_1(\célula_30_vai_1 ));
  \Célula  \célula_31  (
    .ESQUERDA(1'b0), .A(A[0]), .B(B[0]), .VEM_1(1'b0), .in_5(SELETOR), .DIREITA(A[1]), .S(S[0]),
    .VAI_1(\célula_31_vai_1 ));
endmodule

module \Célula_mais_significativa  (
  input  ESQUERDA,
  input  DIREITA,
  input  A,
  input  B,
  input  [4:0] in_5,
  input  VEM_1,
  input  \DIREITA_ARITMÉTICA ,
  output S,
  output VAI_1
);

  wire adder_1_cout, adder_1_out, and_1_out, and_2_out, nand_1_out, or_1_out, subtractor_1_bout,
       subtractor_1_out, xor_1_out;

  and and_1 (and_1_out, A, B);
  or or_1 (or_1_out, A, B);
  nand nand_1 (nand_1_out, A, B);
  xor xor_1 (xor_1_out, A, B);
  Adder #(.width(1)) adder_1 (.a(A), .b(B), .out(adder_1_out), .cin(VEM_1), .cout(adder_1_cout));
  Subtractor #(.width(1)) subtractor_1 (.a(A), .b(B), .out(subtractor_1_out), .bin(VEM_1), .bout(subtractor_1_bout));
  and and_2 (and_2_out, ~in_5[4], ~in_5[3], in_5[2], in_5[1], ~in_5[0]);  // AND_Gate
  Multiplexer multiplexer_1 (.in0(adder_1_cout), .in1(subtractor_1_bout), .out(VAI_1), .sel(and_2_out));  // open: en
  Multiplexer #(.select(5), .enable("false")) multiplexer_2 (
    .in0(and_1_out), .in1(or_1_out), .in2(nand_1_out), .in3(xor_1_out), .in4(adder_1_out), .in5(adder_1_out),
    .in6(subtractor_1_out), .in7(DIREITA), .in8(\DIREITA_ARITMÉTICA ), .in9(ESQUERDA), .out(S), .sel(in_5));  // open: in10, in11, in12, in13, in14, in15, in16, in17, in18, in19, in20, in21, in22, in23, in24, in25, in26, in27, in28, in29, in30, in31
endmodule

module Overflow (
  input  A,
  input  B,
  input  S,
  input  VEM_1,
  input  [4:0] SELETOR,
  output VAI_1
);

  wire and_1_out, and_2_out, or_1_out;

  and and_1 (and_1_out, ~A, S, ~B);  // AND_Gate
  and and_2 (and_2_out, A, ~S, B);  // AND_Gate
  or or_1 (or_1_out, and_1_out, and_2_out);
  Multiplexer #(.select(5), .enable("false")) multiplexer_1 (
    .in0(or_1_out), .in1(VEM_1), .in2(VEM_1), .out(VAI_1), .sel(SELETOR));  // open: in3, in4, in5, in6, in7, in8, in9, in10, in11, in12, in13, in14, in15, in16, in17, in18, in19, in20, in21, in22, in23, in24, in25, in26, in27, in28, in29, in30, in31
endmodule

module Overflow_fora (
  input  A,
  input  B,
  input  S,
  output out_4
);

  wire and_1_out, and_2_out;

  and and_1 (and_1_out, ~A, S, ~B);  // AND_Gate
  and and_2 (and_2_out, A, ~S, B);  // AND_Gate
  or or_1 (out_4, and_1_out, and_2_out);
endmodule

module Shifter (
  input  A31,
  input  A30,
  input  A29,
  input  A28,
  input  A27,
  input  A26,
  input  A25,
  input  A24,
  input  A23,
  input  A22,
  input  A21,
  input  A20,
  input  A19,
  input  A18,
  input  A17,
  input  A16,
  input  A15,
  input  A14,
  input  A13,
  input  A12,
  input  A11,
  input  A10,
  input  A09,
  input  A08,
  input  A07,
  input  A06,
  input  A05,
  input  A04,
  input  A03,
  input  A02,
  input  A01,
  input  A00,
  input  ESQUERDA,
  input  DIREITA,
  output S31,
  output S30,
  output S29,
  output S28,
  output S27,
  output S26,
  output S25,
  output S24,
  output S23,
  output S22,
  output S21,
  output S20,
  output S19,
  output S18,
  output S17,
  output S16,
  output S15,
  output A14_2,
  output S13,
  output S12,
  output S11,
  output S10,
  output S09,
  output S08,
  output S07,
  output S06,
  output S05,
  output S04,
  output S03,
  output S02,
  output S01,
  output S00
);

  Multiplexer #(.select(2), .enable("false")) multiplexer_1 (
    .in0(A31), .in1(A30), .in2(1'b0), .out(S31), .sel({DIREITA, ESQUERDA}));  // open: in3
  Multiplexer #(.select(2), .enable("false")) multiplexer_2 (
    .in0(A30), .in1(A29), .in2(A29), .out(S30), .sel({DIREITA, ESQUERDA}));  // open: in3
  Multiplexer #(.select(2), .enable("false")) multiplexer_3 (
    .in0(A29), .in1(A28), .in2(A30), .out(S29), .sel({DIREITA, ESQUERDA}));  // open: in3
  Multiplexer #(.select(2), .enable("false")) multiplexer_4 (
    .in0(A28), .in1(A27), .in2(A29), .out(S28), .sel({DIREITA, ESQUERDA}));  // open: in3
  Multiplexer #(.select(2), .enable("false")) multiplexer_5 (
    .in0(A27), .in1(A26), .in2(A28), .out(S27), .sel({DIREITA, ESQUERDA}));  // open: in3
  Multiplexer #(.select(2), .enable("false")) multiplexer_6 (
    .in0(A26), .in1(A25), .in2(A27), .out(S26), .sel({DIREITA, ESQUERDA}));  // open: in3
  Multiplexer #(.select(2), .enable("false")) multiplexer_7 (
    .in0(A25), .in1(A24), .in2(A26), .out(S25), .sel({DIREITA, ESQUERDA}));  // open: in3
  Multiplexer #(.select(2), .enable("false")) multiplexer_8 (
    .in0(A24), .in1(A23), .in2(A25), .out(S24), .sel({DIREITA, ESQUERDA}));  // open: in3
  Multiplexer #(.select(2), .enable("false")) multiplexer_9 (
    .in0(A23), .in1(A22), .in2(A24), .out(S23), .sel({DIREITA, ESQUERDA}));  // open: in3
  Multiplexer #(.select(2), .enable("false")) multiplexer_10 (
    .in0(A22), .in1(A21), .in2(A23), .out(S22), .sel({DIREITA, ESQUERDA}));  // open: in3
  Multiplexer #(.select(2), .enable("false")) multiplexer_11 (
    .in0(A21), .in1(A20), .in2(A22), .out(S21), .sel({DIREITA, ESQUERDA}));  // open: in3
  Multiplexer #(.select(2), .enable("false")) multiplexer_12 (
    .in0(A20), .in1(A19), .in2(A21), .out(S20), .sel({DIREITA, ESQUERDA}));  // open: in3
  Multiplexer #(.select(2), .enable("false")) multiplexer_13 (
    .in0(A19), .in1(A18), .in2(A20), .out(S19), .sel({DIREITA, ESQUERDA}));  // open: in3
  Multiplexer #(.select(2), .enable("false")) multiplexer_14 (
    .in0(A18), .in1(A17), .in2(A19), .out(S18), .sel({DIREITA, ESQUERDA}));  // open: in3
  Multiplexer #(.select(2), .enable("false")) multiplexer_15 (
    .in0(A17), .in1(A16), .in2(A18), .out(S17), .sel({DIREITA, ESQUERDA}));  // open: in3
  Multiplexer #(.select(2), .enable("false")) multiplexer_16 (
    .in0(A16), .in1(A15), .in2(A17), .out(S16), .sel({DIREITA, ESQUERDA}));  // open: in3
  Multiplexer #(.select(2), .enable("false")) multiplexer_17 (
    .in0(A15), .in1(A14), .in2(A16), .out(S15), .sel({DIREITA, ESQUERDA}));  // open: in3
  Multiplexer #(.select(2), .enable("false")) multiplexer_18 (
    .in0(A14), .in1(A13), .in2(A15), .out(A14_2), .sel({DIREITA, ESQUERDA}));  // open: in3
  Multiplexer #(.select(2), .enable("false")) multiplexer_19 (
    .in0(A13), .in1(A12), .in2(A14), .out(S13), .sel({DIREITA, ESQUERDA}));  // open: in3
  Multiplexer #(.select(2), .enable("false")) multiplexer_20 (
    .in0(A12), .in1(A11), .in2(A13), .out(S12), .sel({DIREITA, ESQUERDA}));  // open: in3
  Multiplexer #(.select(2), .enable("false")) multiplexer_21 (
    .in0(A11), .in1(A10), .in2(A12), .out(S11), .sel({DIREITA, ESQUERDA}));  // open: in3
  Multiplexer #(.select(2), .enable("false")) multiplexer_22 (
    .in0(A10), .in1(A09), .in2(A11), .out(S10), .sel({DIREITA, ESQUERDA}));  // open: in3
  Multiplexer #(.select(2), .enable("false")) multiplexer_23 (
    .in0(A09), .in1(A08), .in2(A10), .out(S09), .sel({DIREITA, ESQUERDA}));  // open: in3
  Multiplexer #(.select(2), .enable("false")) multiplexer_24 (
    .in0(A08), .in1(A07), .in2(A09), .out(S08), .sel({DIREITA, ESQUERDA}));  // open: in3
  Multiplexer #(.select(2), .enable("false")) multiplexer_25 (
    .in0(A07), .in1(A06), .in2(A08), .out(S07), .sel({DIREITA, ESQUERDA}));  // open: in3
  Multiplexer #(.select(2), .enable("false")) multiplexer_26 (
    .in0(A06), .in1(A05), .in2(A07), .out(S06), .sel({DIREITA, ESQUERDA}));  // open: in3
  Multiplexer #(.select(2), .enable("false")) multiplexer_27 (
    .in0(A05), .in1(A04), .in2(A06), .out(S05), .sel({DIREITA, ESQUERDA}));  // open: in3
  Multiplexer #(.select(2), .enable("false")) multiplexer_28 (
    .in0(A04), .in1(A03), .in2(A05), .out(S04), .sel({DIREITA, ESQUERDA}));  // open: in3
  Multiplexer #(.select(2), .enable("false")) multiplexer_29 (
    .in0(A03), .in1(A02), .in2(A02), .out(S03), .sel({DIREITA, ESQUERDA}));  // open: in3
  Multiplexer #(.select(2), .enable("false")) multiplexer_30 (
    .in0(A02), .in1(A01), .in2(A03), .out(S02), .sel({DIREITA, ESQUERDA}));  // open: in3
  Multiplexer #(.select(2), .enable("false")) multiplexer_31 (
    .in0(A01), .in1(A00), .in2(A02), .out(S01), .sel({DIREITA, ESQUERDA}));  // open: in3
  Multiplexer #(.select(2), .enable("false")) multiplexer_32 (
    .in0(A00), .in1(1'b0), .in2(A01), .out(S00), .sel({DIREITA, ESQUERDA}));  // open: in3
endmodule

module BR (
  input  d3,
  input  d2,
  input  d1,
  input  d0,
  input  WR,
  output s3,
  output s2,
  output s1,
  output s0
);

  D_Flip_Flop d_ff_1 (.clk(d3), .D(WR), .Q(s3));  // open: Qn, preset, en, reset
  D_Flip_Flop d_ff_2 (.clk(d2), .D(WR), .Q(s2));  // open: Qn, preset, en, reset
  D_Flip_Flop d_ff_3 (.clk(d1), .D(WR), .Q(s1));  // open: Qn, preset, en, reset
  D_Flip_Flop d_ff_4 (.clk(d0), .D(WR), .Q(s0));  // open: Qn, preset, en, reset
endmodule

module \BR_continuação  (
  input  in_1,
  input  [31:0] in_2,
  output [31:0] out_3
);

  wire br_1_s0, br_1_s1, br_1_s2, br_2_s0, br_2_s1, br_2_s2, br_3_s0, br_3_s1, br_3_s2, br_4_s0, br_4_s1,
       br_4_s2, br_5_s0, br_5_s1, br_5_s2, br_6_s0, br_6_s1, br_6_s2, br_7_s0, br_7_s1, br_7_s2, br_8_s0,
       br_8_s1, br_8_s2, br_9_s0, br_9_s1, br_9_s2, br_10_s0, br_10_s1, br_10_s2, br_11_s0, br_11_s1,
       br_11_s2, br_12_s0, br_12_s1, br_12_s2, br_13_s0, br_13_s1, br_13_s2, br_14_s2, br_15_s1, br_15_s2,
       br_16_s0, br_16_s1, br_16_s2, br_17_s0, br_17_s1, br_17_s2, br_18_s0, br_18_s1, br_18_s2, br_19_s0,
       br_19_s1, br_19_s2, br_20_s1, br_20_s2, br_21_s0, br_21_s1, br_21_s2, br_22_s1, br_22_s2, br_23_s1,
       br_23_s2, br_24_s0, br_24_s2, br_25_s0, br_25_s1, br_25_s2, br_26_s0, br_26_s1, br_26_s2, br_27_s0,
       br_27_s1, br_27_s2, br_28_s0, br_28_s1, br_29_s0, br_29_s1, br_29_s2, br_30_s0, br_30_s1, br_31_s0,
       br_31_s1, br_31_s2, br_32_s0, br_32_s2, undriven, undriven_2;

  BR br_1 (
    .WR(in_2[0]), .d3(undriven), .d2(undriven_2), .d1(in_1), .d0(in_1), .s3(out_3[0]), .s2(br_1_s2),
    .s1(br_1_s1), .s0(br_1_s0));
  BR br_2 (
    .WR(in_2[1]), .d3(undriven), .d2(undriven_2), .d1(in_1), .d0(in_1), .s3(out_3[1]), .s2(br_2_s2),
    .s1(br_2_s1), .s0(br_2_s0));
  BR br_3 (
    .WR(in_2[2]), .d3(undriven), .d2(undriven_2), .d1(in_1), .d0(in_1), .s3(out_3[2]), .s2(br_3_s2),
    .s1(br_3_s1), .s0(br_3_s0));
  BR br_4 (
    .WR(in_2[3]), .d3(undriven), .d2(undriven_2), .d1(in_1), .d0(in_1), .s3(out_3[3]), .s2(br_4_s2),
    .s1(br_4_s1), .s0(br_4_s0));
  BR br_5 (
    .WR(in_2[4]), .d3(undriven), .d2(undriven_2), .d1(in_1), .d0(in_1), .s3(out_3[4]), .s2(br_5_s2),
    .s1(br_5_s1), .s0(br_5_s0));
  BR br_6 (
    .WR(in_2[5]), .d3(undriven), .d2(undriven_2), .d1(in_1), .d0(in_1), .s3(out_3[5]), .s2(br_6_s2),
    .s1(br_6_s1), .s0(br_6_s0));
  BR br_7 (
    .WR(in_2[6]), .d3(undriven), .d2(undriven_2), .d1(in_1), .d0(in_1), .s3(out_3[6]), .s2(br_7_s2),
    .s1(br_7_s1), .s0(br_7_s0));
  BR br_8 (
    .WR(in_2[7]), .d3(undriven), .d2(undriven_2), .d1(in_1), .d0(in_1), .s3(out_3[7]), .s2(br_8_s2),
    .s1(br_8_s1), .s0(br_8_s0));
  BR br_9 (
    .WR(in_2[8]), .d3(undriven), .d2(undriven_2), .d1(in_1), .d0(in_1), .s3(out_3[8]), .s2(br_9_s2),
    .s1(br_9_s1), .s0(br_9_s0));
  BR br_10 (
    .WR(in_2[9]), .d3(undriven), .d2(undriven_2), .d1(in_1), .d0(in_1), .s3(out_3[9]), .s2(br_10_s2),
    .s1(br_10_s1), .s0(br_10_s0));
  BR br_11 (
    .WR(in_2[10]), .d3(undriven), .d2(undriven_2), .d1(in_1), .d0(in_1), .s3(out_3[10]), .s2(br_11_s2),
    .s1(br_11_s1), .s0(br_11_s0));
  BR br_12 (
    .WR(in_2[11]), .d3(undriven), .d2(undriven_2), .d1(in_1), .d0(in_1), .s3(out_3[11]), .s2(br_12_s2),
    .s1(br_12_s1), .s0(br_12_s0));
  BR br_13 (
    .WR(in_2[12]), .d3(undriven), .d2(undriven_2), .d1(in_1), .d0(in_1), .s3(out_3[12]), .s2(br_13_s2),
    .s1(br_13_s1), .s0(br_13_s0));
  BR br_14 (
    .WR(in_2[13]), .d3(undriven), .d2(undriven_2), .d1(in_1), .d0(in_1), .s3(out_3[13]), .s2(br_14_s2),
    .s1(br_14_s2), .s0(br_14_s2));
  BR br_15 (
    .WR(in_2[14]), .d3(undriven), .d2(undriven_2), .d1(in_1), .d0(in_1), .s3(out_3[14]), .s2(br_15_s2),
    .s1(br_15_s1), .s0(br_15_s1));
  BR br_16 (
    .WR(in_2[15]), .d3(undriven), .d2(undriven_2), .d1(in_1), .d0(in_1), .s3(out_3[15]), .s2(br_16_s2),
    .s1(br_16_s1), .s0(br_16_s0));
  BR br_17 (
    .WR(in_2[16]), .d3(undriven), .d2(undriven_2), .d1(in_1), .d0(in_1), .s3(out_3[16]), .s2(br_17_s2),
    .s1(br_17_s1), .s0(br_17_s0));
  BR br_18 (
    .WR(in_2[17]), .d3(undriven), .d2(undriven_2), .d1(in_1), .d0(in_1), .s3(out_3[17]), .s2(br_18_s2),
    .s1(br_18_s1), .s0(br_18_s0));
  BR br_19 (
    .WR(in_2[18]), .d3(undriven), .d2(undriven_2), .d1(in_1), .d0(in_1), .s3(out_3[18]), .s2(br_19_s2),
    .s1(br_19_s1), .s0(br_19_s0));
  BR br_20 (
    .WR(in_2[19]), .d3(undriven), .d2(undriven_2), .d1(in_1), .d0(in_1), .s3(out_3[19]), .s2(br_20_s2),
    .s1(br_20_s1), .s0(br_20_s1));
  BR br_21 (
    .WR(in_2[20]), .d3(undriven), .d2(undriven_2), .d1(in_1), .d0(in_1), .s3(out_3[20]), .s2(br_21_s2),
    .s1(br_21_s1), .s0(br_21_s0));
  BR br_22 (
    .WR(in_2[21]), .d3(undriven), .d2(undriven_2), .d1(in_1), .d0(in_1), .s3(out_3[21]), .s2(br_22_s2),
    .s1(br_22_s1), .s0(br_22_s1));
  BR br_23 (
    .WR(in_2[22]), .d3(undriven), .d2(undriven_2), .d1(in_1), .d0(in_1), .s3(out_3[22]), .s2(br_23_s2),
    .s1(br_23_s1), .s0(br_23_s1));
  BR br_24 (
    .WR(in_2[23]), .d3(undriven), .d2(undriven_2), .d1(in_1), .d0(in_1), .s3(out_3[23]), .s2(br_24_s2),
    .s1(br_24_s2), .s0(br_24_s0));
  BR br_25 (
    .WR(in_2[24]), .d3(undriven), .d2(undriven_2), .d1(in_1), .d0(in_1), .s3(out_3[24]), .s2(br_25_s2),
    .s1(br_25_s1), .s0(br_25_s0));
  BR br_26 (
    .WR(in_2[25]), .d3(undriven), .d2(undriven_2), .d1(in_1), .d0(in_1), .s3(out_3[25]), .s2(br_26_s2),
    .s1(br_26_s1), .s0(br_26_s0));
  BR br_27 (
    .WR(in_2[26]), .d3(undriven), .d2(undriven_2), .d1(in_1), .d0(in_1), .s3(out_3[26]), .s2(br_27_s2),
    .s1(br_27_s1), .s0(br_27_s0));
  BR br_28 (
    .WR(in_2[27]), .d3(undriven), .d2(undriven_2), .d1(in_1), .d0(in_1), .s3(out_3[27]), .s2(out_3[27]),
    .s1(br_28_s1), .s0(br_28_s0));
  BR br_29 (
    .WR(in_2[28]), .d3(undriven), .d2(undriven_2), .d1(in_1), .d0(in_1), .s3(out_3[28]), .s2(br_29_s2),
    .s1(br_29_s1), .s0(br_29_s0));
  BR br_30 (
    .WR(in_2[29]), .d3(undriven), .d2(undriven_2), .d1(in_1), .d0(in_1), .s3(out_3[29]), .s2(out_3[29]),
    .s1(br_30_s1), .s0(br_30_s0));
  BR br_31 (
    .WR(in_2[30]), .d3(undriven), .d2(undriven_2), .d1(in_1), .d0(in_1), .s3(out_3[30]), .s2(br_31_s2),
    .s1(br_31_s1), .s0(br_31_s0));
  BR br_32 (
    .WR(in_2[31]), .d3(undriven), .d2(undriven_2), .d1(in_1), .d0(in_1), .s3(out_3[31]), .s2(br_32_s2),
    .s1(br_32_s2), .s0(br_32_s0));
endmodule
